# Fritzing sketch loud_loud_boy_device (saved by Fritzing 0.9.3b)

parts:
  OLED_I2C1 = OLED 128x64 I2C Monochrome Display
  U1 = ESP8266 NodeMCU LoLin module
  S1 = Pushbutton [package="[SMD]"]
  R1 = Resistor [tolerance=±5% resistance=100k package="0603 [SMD]"]
  S2 = Pushbutton [package="[SMD]"]
  R2 = Resistor [tolerance=±5% resistance=100k package="0603 [SMD]"]
  J1 = Piezo Speaker
  LED1 = 7-SEGMENT-4DIGIT-YOUNGSUN [package=7-segment-4digit-youngsun-longpads]
  부품1 = Arduino Mega 2560 (Rev3)

nets:
  N1: OLED_I2C1.SDA, U1.D2
  N2: OLED_I2C1.SCK, U1.D1
  VDD: OLED_I2C1.VDD, U1.3V3, S1.Pin_3, S1.Pin_4, S2.Pin_3, S2.Pin_4
  GND: OLED_I2C1.GND, U1.GND, S1.Pin_1, S1.Pin_2, R1.Pin_0, S2.Pin_1, S2.Pin_2, R2.Pin_0, J1.pin1
  N3: U1.D5, R1.Pin_1
  N4: U1.D6, R2.Pin_1
  N5: U1.D7, J1.pin2
  N6: LED1.DIG2, 부품1.D9_PWM
  N7: LED1.D, 부품1.D10_PWM
  N8: LED1.COL-A, 부품1.D6_PWM
  N9: LED1.E, 부품1.D11_PWM
  N10: LED1.DIG3, 부품1.D7_PWM
  N11: LED1.DP, 부품1.D2_PWM
  N12: LED1.APOS-A, 부품1.D12_PWM
  N13: LED1.F, 부품1.D3_PWM
  N14: LED1.COL-C, 부품1.D4_PWM
  N15: LED1.C, 부품1.D8_PWM
  N16: LED1.A, 부품1.D13_PWM
  N17: LED1.G, 부품1.D5_PWM

custom parts:
  ESP8266 NodeMCU LoLin module: ESP8266 based NodeMCU
